# Fritzing sketch AlexaBridge (saved by Fritzing 0.9.3b)
circuit board: 7.5cm x 10cm
breadboards: 2

parts:
  U1 = ESP32-38PinWide [part_number=ESP32-38PinWide]
  Bauteil1 = Adafruit PCA9685 PWM/Servo Breakout [part_number=815]
  Bauteil2 = INMP441
  U2 = SBX DSUN [package=THT]
  J1 = Screw terminal - 2 pins [package=THT]
  S1 = Pushbutton [package="[THT]"]
  VCC1 = Battery block 9V
  R1 = Resistor [tolerance=±2% resistance=1k package=THT]

nets:
  N1: U1.3.3, Bauteil2.VDD, S1.Pin_1, S1.Pin_2
  N2: U1.GPIO32, Bauteil1.SDA
  N3: U1.GPIO33, Bauteil1.SCL
  GND: U1.GND, Bauteil1.GND, Bauteil2.L/R, Bauteil2.GND, U2.GND, J1.pin1, VCC1.-, R1.Pin_0
  VIN: U1.VIN, Bauteil1.5.0V, Bauteil1.VCC, U2.+VOUT
  N4: U1.GPIO4, S1.Pin_3, S1.Pin_4, R1.Pin_1
  N5: U1.GPIO21, Bauteil2.SD
  N6: U1.GPIO22, Bauteil2.SCK
  N7: U1.GPIO23, Bauteil2.WS
  N8: U2.+VIN, J1.pin2, VCC1.+

custom parts:
  ESP32-38PinWide: Generic 38-Pin ESP32 with wide format (only access to one side of pins on a breadboard) based on Stephen Lilley's HiLetgo ESP-WROOM-32 ESP32 ESP-32S Development Board.
  Adafruit PCA9685 PWM/Servo Breakout: Using only two pins, control 16 free-running PWM outputs! I2C-controlled PWM driver with a built in clock. Unlike the TLC5940 family, you do not need to continuously send it signal tying up your microcontroller, its completely free running! 5V compliant, which means you can control it from a 3.3V microcontroller and still safely drive up to 6V outputs (this is good for when you want to control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
  INMP441: This is a simple breakout board for the INMP441 I2S MEMS microphone.
  SBX DSUN: SBX DSUN input voltage 4.5 - 28V DC output voltage .8v to 20VDC (step down converter) Output current 3A max
